# Fritzing sketch all (saved by Fritzing 0.9.1b)
circuit board: 8.46667cm x 5.64444cm
breadboards: 1

parts:
  元件1 = Arduino Uno (Rev3)
  IC1 = ULN2003A [package="SO16 [SMD]"]
  LED1 = smd LED [color="Red (633nm)" package="1206 [SMD]"]
  LED2 = smd LED [color="Red (633nm)" package="1206 [SMD]"]
  LED3 = smd LED [color="Red (633nm)" package="1206 [SMD]"]
  U1 = LIPO-1000mAh [package=lipo-1000]
  元件3 = IMU Digital Combo Board 6DOF
  元件6 = Barometric Pressure Sensor - BMP085 Breakout
  元件7 = IMU Digital Combo Board 6DOF
  IC2 = IC, DIP package, 8 pins [chip_label=EV3]

nets:
  N1: 元件1.A4/SDA, 元件3.SDA, 元件6.SCL, 元件7.SDA
  N2: 元件1.A5/SCL, 元件3.SCL, 元件6.SDA, 元件7.SCL
  N3: 元件1.D11_PWM/MOSI, IC1.In_3
  N4: 元件1.D12/MISO, IC1.In_2
  N5: 元件1.D13/SCK, IC1.In_1
  GND: 元件1.GND, IC1.0V, U1.-, 元件3.GND, 元件6.GND, 元件7.GND
  N6: 元件1.D5_PWM, IC2.pin2
  N7: 元件1.D6_PWM, IC2.pin1
  3.3V: 元件1.3V3, 元件3.3.3V, 元件6.VCC, 元件7.3.3V
  N8: IC1.Out_3, LED3.cathode
  N9: IC1.Out_2, LED2.cathode
  N10: IC1.Out_1, LED1.cathode
  N11: LED1.anode, LED2.anode, LED3.anode, U1.+
  N12: 元件3.INT1, 元件7.INT1
  N13: 元件3.INT0, 元件7.INT0
