# Fritzing sketch arduino (saved by Fritzing 0.9.1b)
perfboards: 1

parts:
  元件1 = Arduino Pro Mini v13
  J1 = female pin header, 8 pins [form="♀ (female)"]
  J2 = female pin header, 3 pins [form="♀ (female)"]
  IC1 = ULN2003A [package="SO16 [SMD]"]
  LED1 = LED - 5mm [color="Red (660nm)" package="5 mm [THT]"]  # not connected
  J6 = male pin header, 2 pins [form="♂ (male)"]
  J7 = male pin header, 2 pins [form="♂ (male)"]
  VCC1 = Battery
  LED2 = LED - 5mm [color="Red (633nm)" package="5 mm [THT]"]
  J8 = female pin header, 2 pins [form="♀ (female)"]
  J9 = female pin header, 2 pins [form="♀ (female)"]
  J10 = female pin header, 2 pins [form="♀ (female)"]
  J11 = female pin header, 2 pins [form="♀ (female)"]

nets:
  N1: 元件1.A4, J1.pin4, J2.pin2
  N2: 元件1.A5, J1.pin3, J2.pin3
  N3: 元件1.GND, J1.pin2, J6.pin1, VCC1.-, J11.pin1
  N4: 元件1.VCC, J1.pin1, J1.pin7, J7.pin2, LED2.anode
  N5: 元件1.D13/SCK, IC1.In_1
  N6: 元件1.D12/MISO, IC1.In_3
  N7: 元件1.D9_PWM, J11.pin2
  N8: 元件1.D6_PWM, J10.pin2
  N9: 元件1.D5_PWM, J9.pin2
  N10: 元件1.D3_PWM, J8.pin2
  N11: IC1.Out_3, J7.pin1, LED2.cathode
  N12: IC1.Out_1, J6.pin2
