# Fritzing sketch bt (saved by Fritzing 0.9.1b)
breadboards: 1

parts:
  元件1 = Bluetooth HC-05 Macho
  元件2 = Arduino Uno (Rev3)
  J1 = Basic Servo

nets:
  N1: 元件1.TXD, 元件2.D10_PWM/SS
  N2: 元件1.RXD, 元件2.D11_PWM/MOSI
  VCC: 元件1.VCC, 元件2.VIN, J1.vcc
  GND: 元件1.GND, 元件2.GND, J1.gnd
  N3: 元件2.D9_PWM, J1.pulse
