# Fritzing sketch gyro (saved by Fritzing 0.9.1b)

parts:
  元件1 = Arduino Uno (Rev3)
  元件2 = Arduino Uno (Rev3)
  元件5 = IMU Digital Combo Board 6DOF

nets:
  N1: 元件1.A4/SDA, 元件5.SDA
  N2: 元件1.A5/SCL, 元件5.SCL
  N3: 元件1.D10_PWM/SS, 元件2.D11_PWM/MOSI
  N4: 元件1.D11_PWM/MOSI, 元件2.D10_PWM/SS
  3V3: 元件1.3V3, 元件5.3.3V
  GND: 元件1.GND, 元件2.GND, 元件5.GND
