# Fritzing sketch i2c (saved by Fritzing 0.9.1b)
breadboards: 1

parts:
  元件1 = Arduino Uno (Rev3)
  元件2 = Arduino Uno (Rev3)
  J1 = Basic Servo
  R1 = Rotary Potentiometer (Small) [maximum_resistance=100kΩ package=THT]
  LED1 = LED - 5mm [color="Red (633nm)" package="5 mm [THT]"]
  R2 = Resistor [tolerance=±5% resistance=10k package=THT]
  R3 = Resistor [tolerance=±5% resistance=220 package=THT]

nets:
  N1: 元件1.A4/SDA, 元件2.A4/SDA
  N2: 元件1.A5/SCL, 元件2.A5/SCL
  N3: 元件1.D9_PWM, J1.pulse
  GND: 元件1.GND, 元件2.GND, J1.gnd, R1.leg1, LED1.cathode
  VIN: 元件1.VIN, J1.vcc
  N4: 元件2.A0, R1.wiper
  N5: 元件2.D13/SCK, R3.Pin_1
  N6: 元件2.5V, R2.Pin_1
  N7: R1.leg2, R2.Pin_0
  N8: LED1.anode, R3.Pin_0
