# Fritzing sketch motor (saved by Fritzing 0.9.1b)
circuit board: 8.46667cm x 5.64444cm
breadboards: 1

parts:
  D1 = Rectifier Diode [part_number=1N4001 package="300 mil [THT]"]
  R1 = Resistor [tolerance=±5% resistance=220 package=THT]
  D2 = Rectifier Diode [part_number=1N4001 package="300 mil [THT]"]
  R2 = Resistor [tolerance=±5% resistance=220 package=THT]
  D3 = Rectifier Diode [part_number=1N4001 package="300 mil [THT]"]
  R3 = Resistor [tolerance=±5% resistance=220 package=THT]
  D4 = Rectifier Diode [part_number=1N4001 package="300 mil [THT]"]
  R4 = Resistor [tolerance=±5% resistance=220 package=THT]
  J1 = female pin header, 2 pins [form="♀ (female)"]
  J2 = female pin header, 2 pins [form="♀ (female)"]
  J3 = female pin header, 2 pins [form="♀ (female)"]
  J5 = female pin header, 2 pins [form="♀ (female)"]
  J6 = female pin header, 2 pins [form="♀ (female)"]
  J7 = female pin header, 2 pins [form="♀ (female)"]
  J8 = female pin header, 2 pins [form="♀ (female)"]
  J4 = female pin header, 2 pins [form="♀ (female)"]

nets:
  N1: D1.cathode, R1.Pin_1, J1.pin1
  N2: D1.anode, J1.pin2, J2.pin2
  N3: R1.Pin_0, J2.pin1
  N4: D2.cathode, R2.Pin_1, J3.pin1
  N5: D2.anode, J3.pin2, J4.pin2
  N6: R2.Pin_0, J4.pin1
  N7: D3.cathode, R3.Pin_1, J5.pin1
  N8: D3.anode, J5.pin2, J6.pin2
  N9: R3.Pin_0, J6.pin1
  N10: D4.cathode, R4.Pin_1, J7.pin1
  N11: D4.anode, J7.pin2, J8.pin2
  N12: R4.Pin_0, J8.pin1
