# Fritzing sketch rc_boat (saved by Fritzing 0.9.1b)
breadboards: 1

parts:
  元件2 = Arduino Uno (Rev3)
  left_motor = Basic Servo
  right_motor = Basic Servo
  HC-05 = Bluetooth HC-05 Macho

nets:
  N1: 元件2.D10_PWM/SS, HC-05.TXD
  N2: 元件2.D11_PWM/MOSI, HC-05.RXD
  N3: 元件2.D5_PWM, right_motor.pulse
  N4: 元件2.D6_PWM, left_motor.pulse
  5V: 元件2.5V, HC-05.VCC
  GND: 元件2.GND, left_motor.gnd, right_motor.gnd, HC-05.GND
  VCC: 元件2.VIN, left_motor.vcc, right_motor.vcc
