# Fritzing sketch uln2003 (saved by Fritzing 0.9.1b)
breadboards: 1

parts:
  元件1 = Arduino Uno (Rev3)
  IC1 = ULN2003A [package="DIP16 [THT]"]
  VCC1 = Battery
  LED1 = LED - 5mm [color="Red (633nm)" package="5 mm [THT]"]

nets:
  N1: 元件1.D13/SCK, IC1.In_1
  N2: 元件1.GND, IC1.0V, VCC1.-
  N3: IC1.Out_1, LED1.cathode
  N4: VCC1.+, LED1.anode
