# Fritzing sketch waterbot (saved by Fritzing 0.9.1b)
breadboards: 1

parts:
  元件1 = Intel Edison Arduinobreakout
  元件2 = Motor Driver 1A Dual TB6612FNG
  IC1 = ULN2003A [package="DIP16 [THT]"]
  VCC1 = Battery
  LED1 = LED - 5mm [color="Red (633nm)" package="5 mm [THT]"]
  M1 = DC Motor

nets:
  N1: 元件1.D8, IC1.In_1
  GND: 元件1.GND, 元件2.GND, IC1.0V, VCC1.-
  N2: 元件1.D3_PWM, 元件2.PWMA
  N3: 元件1.D4, 元件2.AIN2
  N4: 元件1.D5_PWM, 元件2.AIN1
  N5: 元件1.D6_PWM, 元件2.STBY
  N6: 元件2.A02, M1.pin_1
  N7: 元件2.A01, M1.pin_2
  N8: 元件2.VM, VCC1.+, LED1.anode
  N9: IC1.Out_1, LED1.cathode
